# Fritzing sketch 2x-MAX7219-matriz-led (saved by Fritzing 0.8.7b)
breadboards: 1

parts:
  Part1 = Arduino Uno (Rev3)
  Part2 = LED Matrix - Serial Interface - Red/Green/Blue
  Part3 = LED Matrix - Serial Interface - Red/Green/Blue

nets:
  N1: Part1.D10_PWM/SS, Part2.CS, Part3.CS
  N2: Part1.D11_PWM/MOSI, Part2.SCK, Part3.SCK
  N3: Part1.D12/MISO, Part2.MOSI
  VCC: Part1.3V3, Part2.VCC, Part3.VCC
  GND: Part1.GND, Part2.GND, Part3.GND
  N4: Part2.MISO, Part3.MOSI
