# Fritzing sketch clock-DS1307 (saved by Fritzing 0.8.7b)

parts:
  U1 = DS1307 [package=so08]
  Part1 = Arduino Uno (Rev3)

nets:
  GND: U1.GND, Part1.GND
  N1: U1.SDA, Part1.A4/SDA
  N2: U1.SCL, Part1.A5/SCL
  VCC: U1.VCC, Part1.5V
